// Logisim project lab01_65070162 XOR Project.circ as structural Verilog: 2 circuits, main circuit myXOR
module myXOR (
  input  A,
  input  B,
  output Z
);

  wire and_1_out, and_2_out, not_1_out, not_2_out;

  not not_1 (not_1_out, A);
  not not_2 (not_2_out, B);
  and and_1 (and_1_out, A, not_2_out);
  and and_2 (and_2_out, not_1_out, B);
  or or_1 (Z, and_1_out, and_2_out);
endmodule

module sub_curcuit (
  input  B5,
  input  B4,
  input  B3,
  input  B2,
  input  B1,
  input  B0,
  output LED
);

  wire XOR_2_z, XOR_3_z, XOR_4_z, XOR_z;

  myXOR XOR (.A(B5), .B(B4), .Z(XOR_z));
  myXOR XOR_2 (.A(B3), .B(B2), .Z(XOR_2_z));
  myXOR XOR_3 (.A(B1), .B(B0), .Z(XOR_3_z));
  myXOR XOR_4 (.A(XOR_z), .B(XOR_2_z), .Z(XOR_4_z));
  myXOR XOR_5 (.A(XOR_4_z), .B(XOR_3_z), .Z(LED));
endmodule
