// Logisim project lab01_65070162 myXNOR.circ as structural Verilog: 3 circuits, main circuit myXNOR
module myXNOR (
  input  A,
  input  B,
  output Z
);

  wire and_1_out, and_2_out, not_1_out, not_2_out;

  not not_1 (not_1_out, A);
  not not_2 (not_2_out, B);
  and and_1 (and_1_out, not_1_out, not_2_out);
  and and_2 (and_2_out, A, B);
  or or_1 (Z, and_1_out, and_2_out);
endmodule

module _4b_cmp (
  input  A3,
  input  A2,
  input  A1,
  input  A0,
  input  B3,
  input  B2,
  input  B1,
  input  B0,
  output W
);

  wire and_1_out, and_2_out, myXNOR_2_z, myXNOR_3_z, myxnor_4_z, myXNOR_z;

  myXNOR myXNOR (.A(A3), .B(B3), .Z(myXNOR_z));
  myXNOR myXNOR_2 (.A(A2), .B(B2), .Z(myXNOR_2_z));
  myXNOR myXNOR_3 (.A(A1), .B(B1), .Z(myXNOR_3_z));
  myXNOR myxnor_4 (.A(A0), .B(B0), .Z(myxnor_4_z));
  and and_1 (and_1_out, myXNOR_z, myXNOR_2_z);
  and and_2 (and_2_out, myXNOR_3_z, myxnor_4_z);
  and and_3 (W, and_1_out, and_2_out);
endmodule

module main (
  input  A3,
  input  A2,
  input  A1,
  input  A0,
  input  B3,
  input  B2,
  input  B1,
  input  B0,
  output W
);

  _4b_cmp _4_bit_comparator (.A3(A3), .A2(A2), .A1(A1), .A0(A0), .B3(B3), .B2(B2), .B1(B1), .B0(B0), .W(W));
endmodule
