// Logisim project lab03_65070162 Boolean Minimization.circ as structural Verilog: 2 circuits, main circuit First Full Circuit
module First_Full_Circuit (
  input  W,
  input  X,
  input  Y,
  input  Z,
  output F
);

  wire and_1_out, and_2_out, and_3_out, and_4_out, and_5_out, not_1_out, not_2_out, not_3_out;

  not not_1 (not_1_out, W);
  not not_2 (not_2_out, Y);
  not not_3 (not_3_out, Z);
  and and_1 (and_1_out, W, X);
  and and_2 (and_2_out, W, X, Y);
  and and_3 (and_3_out, not_1_out, Y, Z);
  and and_4 (and_4_out, not_1_out, not_2_out, Z);
  and and_5 (and_5_out, not_1_out, X, Y, not_3_out);
  or or_1 (F, and_1_out, and_2_out, and_3_out, and_4_out, and_5_out);
endmodule

module First_Minimize (
  input  W,
  input  X,
  input  Y,
  input  Z,
  output F
);

  wire and_1_out, and_2_out, and_3_out, not_1_out, not_2_out;

  not not_1 (not_1_out, W);
  not not_2 (not_2_out, Z);
  and and_1 (and_1_out, W, X);
  and and_2 (and_2_out, not_1_out, Z);
  and and_3 (and_3_out, not_1_out, X, Y, not_2_out);
  or or_1 (F, and_1_out, and_2_out, and_3_out);
endmodule
