// Logisim project lab02_65070162 Nested Gate.circ as structural Verilog: 2 circuits, main circuit Basic Gate
module Basic_Gate (
  input  A,
  input  B,
  input  A_2,
  input  B_2,
  input  A_3,
  input  A_4,
  input  B_3,
  input  A_5,
  input  B_4,
  output Output,
  output Output_2,
  output Output_3,
  output Output_4,
  output Output_5
);

  or or_1 (Output, A, B);
  and and_1 (Output_2, A_2, B_2);
  not not_1 (Output_3, A_3);
  nand nand_1 (Output_4, A_4, B_3);
  nor nor_1 (Output_5, A_5, B_4);
endmodule

module Nested (
  input  A,
  input  B,
  input  C,
  input  A_2,
  input  B_2,
  input  C_2,
  input  A_3,
  input  B_3,
  input  C_3,
  input  A_4,
  input  B_4,
  input  C_4,
  output Y,
  output Y_2,
  output Y_3,
  output Y_4
);

  wire and_1_out, nand_1_out, nor_1_out, or_1_out;

  or or_1 (or_1_out, A, B);
  and and_1 (and_1_out, A_2, B_2);
  nor nor_1 (nor_1_out, A_3, B_3);
  nand nand_1 (nand_1_out, A_4, B_4);
  or or_2 (Y, or_1_out, C);
  and and_2 (Y_2, and_1_out, C_2);
  nor nor_2 (Y_3, nor_1_out, C_3);
  nand nand_2 (Y_4, nand_1_out, C_4);
endmodule
