// Logisim project lab01_65070162 Sub Curcuit.circ as structural Verilog: 2 circuits, main circuit main
// XOR
module myXOR (
  input  A,
  input  B,
  output Z
);

  wire and_1_out, and_2_out, not_1_out, not_2_out;

  not not_1 (not_1_out, A);
  not not_2 (not_2_out, B);
  and and_1 (and_1_out, A, not_2_out);
  and and_2 (and_2_out, not_1_out, B);
  or or_1 (Z, and_1_out, and_2_out);
endmodule

module main (
  input  _5,
  input  _4,
  input  _3,
  input  _2,
  input  _1,
  input  _0,
  output LED
);

  wire myxor_1_z, myxor_2_z, myxor_3_z, myxor_4_z;

  myXOR myxor_1 (.A(_5), .B(_4), .Z(myxor_1_z));
  myXOR myxor_2 (.A(_3), .B(_2), .Z(myxor_2_z));
  myXOR myxor_3 (.A(_1), .B(_0), .Z(myxor_3_z));
  myXOR myxor_4 (.A(myxor_1_z), .B(myxor_2_z), .Z(myxor_4_z));
  myXOR myxor_5 (.A(myxor_4_z), .B(myxor_3_z), .Z(LED));
endmodule
